# Fritzing sketch ArduinoSketch (saved by Fritzing 0.9.5d)
breadboards: 1

parts:
  부품1 = Arduino Uno (Rev3) - ICSP
  부품2 = Adafruit PN532 Breakout [part_number="Adafruit #364"]
  U1 = LCD-16X2 [package=lcd-16x2]  # not connected
  M1 = pcf8574 io expansion board [package=THT]

nets:
  N1: 부품1.A4/SDA, M1.SDA
  N2: 부품1.A5/SCL, M1.SCL
  N3: 부품1.D2, 부품2.SCK
  N4: 부품1.D3_PWM, 부품2.MOSI/SDA/TX
  N5: 부품1.D4, 부품2.NSS/SCL/RX
  N6: 부품1.D5_PWM, 부품2.MISO
  5V: 부품1.5V, 부품2.+5.0V, M1.VCC
  GND: 부품1.GND, 부품2.GND, M1.GND

custom parts:
  Adafruit PN532 Breakout: The PN532 is the most popular NFC chip, and is what is embedded in pretty much every phone or device that does NFC. It can pretty much do it all, such as read and write to tags and cards, communicate with phones (say for payment processing), and 'act' like a NFC tag. If you want to do any sort of embedded NFC work, this is the chip you'll want to use! NFC (Near Field Communications) is a way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
  pcf8574 io expansion board: pcf8574 io expansion board.
